// Logisim project ddcaco1  (2).circ as structural Verilog: 1 circuit, main circuit main
module main (
  input  in_1,
  input  in_2,
  input  in_3,
  input  in_4
);

  wire and_1_out, and_2_out, and_4_out, and_6_out, and_8_out, and_9_out, and_10_out, not_1_out, not_3_out,
       or_1_out, or_2_out, or_3_out, or_4_out, or_5_out, or_6_out, or_7_out;

  not not_1 (not_1_out, in_1);
  not not_2 (not_1_out, in_1);
  not not_3 (not_3_out, in_1);
  not not_4 (not_3_out, in_1);
  and and_1 (and_1_out, not_1_out, not_1_out, in_1);
  and and_2 (and_2_out, in_1, not_3_out, in_1);
  and and_3 (and_1_out, in_1, not_1_out, not_1_out);
  and and_4 (and_4_out, not_1_out, not_3_out, not_1_out);
  and and_5 (and_1_out, in_1, in_1, not_1_out);
  and and_6 (and_6_out, in_1, in_1, not_1_out);
  and and_7 (and_1_out, not_3_out, in_1, not_1_out);
  and and_8 (and_8_out, not_3_out, in_1, in_1);
  and and_9 (and_9_out, not_1_out, in_1, in_1);
  and and_10 (and_10_out, in_1, in_1, in_1);
  or or_1 (or_1_out, and_1_out, and_1_out, and_1_out, and_8_out, and_9_out);
  or or_2 (or_2_out, and_2_out, and_1_out, and_1_out, and_1_out, and_1_out);
  or or_3 (or_3_out, and_10_out, and_1_out, and_1_out, and_1_out, and_1_out);
  or or_4 (or_4_out, and_1_out, and_1_out, and_1_out, and_6_out, and_4_out);
  or or_5 (or_5_out, and_1_out, and_1_out, and_1_out, and_1_out, and_9_out);
  or or_6 (or_6_out, and_9_out, and_1_out, and_1_out, and_1_out, and_1_out);
  or or_7 (or_7_out, and_1_out, and_1_out, and_8_out, and_1_out, and_10_out);
  _7_Segment_Display #(.active("false")) u_7_segment_display_1 (
    .g(or_3_out), .f(or_2_out), .a(or_1_out), .b(1'b0), .e(or_4_out), .d(or_5_out), .c(or_6_out),
    .dp(or_7_out));

  assign in_2 = in_1;
  assign in_3 = in_1;
  assign in_4 = in_1;

  // Notes on the sheet:
  //   d0
  //   d1
  //   D2
  //   D3
  //   D4
  //   D5
  //   D6
  //   D7
  //   D8
  //   D9
endmodule
