// Logisim project finallll.circ as structural Verilog: 1 circuit, main circuit main
module main (
  input  in_1,
  input  in_2,
  input  in_3,
  input  in_4,
  input  in_5,
  input  in_6,
  input  in_7,
  input  in_8,
  input  in_9,
  output out_10,
  output out_11,
  output out_12,
  output out_13
);

  wire xor_1_out, xor_2_out, xor_3_out, xor_4_out;

  xor xor_1 (xor_1_out, in_1, in_9);
  xor xor_2 (xor_2_out, in_2, in_9);
  xor xor_3 (xor_3_out, in_7, in_9);
  xor xor_4 (xor_4_out, in_8, in_9);
  BitAdder #(.width(1)) bitadder_1 (
    .in0(in_3), .in1(xor_1_out), .in2(in_4), .in3(xor_2_out), .in4(in_5), .in5(xor_3_out), .in6(in_6),
    .in7(xor_4_out), .in8(in_9), .out({out_13, out_12, out_11, out_10}));
endmodule
